# Fritzing sketch ESP32-app-board (saved by Fritzing 1.0.6)
circuit board: 8cm x 5.5cm

parts:
  R12 = Resistor [tolerance=±5% power=0.25W resistance=100 package=THT]
  R13 = Resistor [tolerance=±5% power=0.25W resistance=100 package=THT]
  Buzzer = Piezo Buzzer
  ZS-042 = ZS-042 Real Time Clock Module
  Ports = male pin header, 15 pins [form="♂ (male)"]
  Ports_2 = male pin header, 15 pins [form="♂ (male)"]
  3V3 = male pin header, 2 pins [form="♂ (male)"]
  R14 = Resistor [tolerance=±5% power=0.25W resistance=100 package=THT]
  R27 = Resistor [tolerance=±5% power=0.25W resistance=100 package=THT]
  R26 = Resistor [tolerance=±5% power=0.25W resistance=100 package=THT]
  GND = male pin header, 4 pins [form="♂ (male)"]
  +5V = male pin header, 4 pins [form="♂ (male)"]
  GND_2 = male pin header, 2 pins [form="♂ (male)"]
  I2C = male pin header, 4 pins [form="♂ (male)"]
  Matrix1 = male pin header, 8 pins [form="♂ (male)"]
  Matrix2 = male pin header, 8 pins [form="♂ (male)"]
  Matrix3 = male pin header, 8 pins [form="♂ (male)"]
  Matrix4 = male pin header, 8 pins [form="♂ (male)"]
  Matrix5 = male pin header, 8 pins [form="♂ (male)"]
  Matrix6 = male pin header, 8 pins [form="♂ (male)"]
  ESP32-WROOM-32 = ESP32-WROOM-32 [part_number=ESP32S-PIN30]
  3V3_2 = male pin header, 1 pin [form="♂ (male)"]
  GND_3 = male pin header, 1 pin [form="♂ (male)"]
  +5V_2 = male pin header, 1 pin [form="♂ (male)"]
  Btn = SWITCH-MOMENTARY-2 [package=tactile-pth]
  Vin = Terminal Block - 2 pins [package=THT]
  Button = male pin header, 2 pins [form="♂ (male)"]
  LED = RGB LED (com. anode, rbg) [color="Red (633nm)" current=0.030A package="5 mm [THT]"]
  LED_2 = male pin header, 3 pins [form="♂ (male)"]
  Pad1 = Pad [width=2 height=3.2 connect=north]
  Pad2 = Pad [width=2 height=3.2 connect=north]
  Pad3 = Pad [width=2 height=3.2 connect=north]
  Pad4 = Pad [width=2 height=3.2 connect=north]
  Pad5 = Pad [width=2 height=3.2 connect=north]
  Pad6 = Pad [width=2 height=3.2 connect=north]
  Pad7 = Pad [width=2 height=3.2 connect=north]
  Pad8 = Pad [width=2 height=3.2 connect=north]
  Pad9 = Pad [width=2 height=3.2 connect=north]
  Pad10 = Pad [width=2 height=3.2 connect=north]
  Pad11 = Pad [width=2 height=3.2 connect=north]
  Pad12 = Pad [width=2 height=3.2 connect=north]
  Pad13 = Pad [width=2 height=3.2 connect=north]
  Pad14 = Pad [width=2 height=3.2 connect=north]
  Pad15 = Pad [width=2 height=3.2 connect=north]
  Pad16 = Pad [width=2 height=3.2 connect=south]
  Pad17 = Pad [width=2 height=3.2 connect=south]
  Pad18 = Pad [width=2 height=3.2 connect=south]
  Pad19 = Pad [width=2 height=3.2 connect=south]
  Pad20 = Pad [width=2 height=3.2 connect=south]
  Pad21 = Pad [width=2 height=3.2 connect=south]
  Pad22 = Pad [width=2 height=3.2 connect=south]
  Pad23 = Pad [width=2 height=3.2 connect=south]
  Pad24 = Pad [width=2 height=3.2 connect=south]
  Pad25 = Pad [width=2 height=3.2 connect=south]
  Pad26 = Pad [width=2 height=3.2 connect=south]
  Pad27 = Pad [width=2 height=3.2 connect=south]
  Pad28 = Pad [width=2 height=3.2 connect=south]
  Pad29 = Pad [width=2 height=3.2 connect=south]
  Pad30 = Pad [width=2 height=3.2 connect=south]
  Pad31 = Pad [width=2 height=3.2 connect=south]
  Pad32 = Pad [width=2 height=3.2 connect=south]
  Pad33 = Pad [width=2 height=3.2 connect=south]
  Pad34 = Pad [width=2 height=3.2 connect=south]
  Pad35 = Pad [width=2 height=3.2 connect=south]
  Pad36 = Pad [width=2 height=3.2 connect=south]
  Pad37 = Pad [width=2 height=3.2 connect=north]
  Pad38 = Pad [width=2 height=3.2 connect=north]
  Pad39 = Pad [width=2 height=3.2 connect=north]
  Pad40 = Pad [width=2 height=3.2 connect=north]
  Pad41 = Pad [width=2 height=3.2 connect=north]
  Pad42 = Pad [width=2 height=3.2 connect=north]

nets:
  N1: R12.Pin_0, Ports_2.pin12, LED.blue_cathode, Pad19.pad
  N2: R12.Pin_1, ESP32-WROOM-32.D12
  N3: R13.Pin_0, Ports_2.pin13, LED.red_cathode, Pad18.pad
  N4: R13.Pin_1, ESP32-WROOM-32.D13
  N5: Buzzer.pin_1, Ports.pin1, ESP32-WROOM-32.D23, Pad15.pad
  GND: Buzzer.pin_2, ZS-042.GND, Ports.pin14, Ports_2.pin14, GND.pin1, GND.pin2, GND.pin3, GND.pin4, GND_2.pin1, GND_2.pin2, I2C.pin1, ESP32-WROOM-32.GND, GND_3.pin1, Btn.2, Vin.Line_1, Button.pin2, LED_2.pin3, Pad2.pad, Pad17.pad, Pad31.pad, Pad36.pad
  N6: ZS-042.SCL, Ports.pin2, I2C.pin4, ESP32-WROOM-32.D22, Pad14.pad, Pad33.pad
  N7: ZS-042.SDA, Ports.pin5, I2C.pin3, ESP32-WROOM-32.D21, Pad11.pad, Pad34.pad
  VCC: ZS-042.VCC, Ports.pin15, 3V3.pin1, 3V3.pin2, I2C.pin2, ESP32-WROOM-32.3V3, 3V3_2.pin1, Pad1.pad, Pad35.pad
  N8: Ports.pin3, ESP32-WROOM-32.TX0, Pad13.pad
  N9: Ports.pin4, ESP32-WROOM-32.RX0, Pad12.pad
  N10: Ports.pin6, ESP32-WROOM-32.D19, Pad10.pad
  N11: Ports.pin7, ESP32-WROOM-32.D18, Pad9.pad
  N12: Ports.pin8, ESP32-WROOM-32.D5, Pad8.pad
  N13: Ports.pin9, ESP32-WROOM-32.TX2, Pad7.pad
  N14: Ports.pin10, ESP32-WROOM-32.RX2, Pad6.pad
  N15: Ports.pin11, ESP32-WROOM-32.D4, Pad5.pad
  N16: Ports.pin12, ESP32-WROOM-32.D2, Pad4.pad
  N17: Ports.pin13, ESP32-WROOM-32.D15, Pad3.pad
  N18: Ports_2.pin1, ESP32-WROOM-32.EN, Pad30.pad
  N19: Ports_2.pin2, ESP32-WROOM-32.VP, Pad29.pad
  N20: Ports_2.pin3, ESP32-WROOM-32.VN, Pad28.pad
  N21: Ports_2.pin4, ESP32-WROOM-32.D34, Pad27.pad
  N22: Ports_2.pin5, ESP32-WROOM-32.D35, Pad26.pad
  N23: Ports_2.pin6, ESP32-WROOM-32.D32, Btn.1, Button.pin1, Pad25.pad, Pad32.pad
  N24: Ports_2.pin7, ESP32-WROOM-32.D33, Pad24.pad
  N25: Ports_2.pin8, ESP32-WROOM-32.D25, Pad23.pad
  N26: Ports_2.pin9, R26.Pin_0, Pad22.pad
  N27: Ports_2.pin10, R27.Pin_0, Pad21.pad
  N28: Ports_2.pin11, R14.Pin_0, LED.green_cathode, Pad20.pad
  N29: Ports_2.pin15, +5V.pin1, +5V.pin2, +5V.pin3, +5V.pin4, ESP32-WROOM-32.Vin, +5V_2.pin1, Vin.Line_2, LED_2.pin1, Pad16.pad
  N30: R14.Pin_1, ESP32-WROOM-32.D14
  N31: R27.Pin_1, ESP32-WROOM-32.D27
  N32: R26.Pin_1, ESP32-WROOM-32.D26
  N33: Matrix1.pin1, Pad42.pad
  N34: Matrix2.pin1, Pad41.pad
  N35: Matrix3.pin1, Pad40.pad
  N36: Matrix4.pin1, Pad39.pad
  N37: Matrix5.pin1, Pad38.pad
  N38: Matrix6.pin1, Pad37.pad
  N39: LED.common_anode, LED_2.pin2

notes:
  +
  +5V
  GND
  SCL
  SDA
  VCC
  ESP32 App Board v1
  Reset
  Flash
  github.com/balassy/esp32-app-board
  CC
  CA

custom parts:
  Piezo Buzzer: Part from https://www.nutsvolts.com/magazine/article/november2012_SmileysWorkshop. Breadboard and icon images modified to be 0.3" in spacing and be more similar to the actual physical part.
  ZS-042 Real Time Clock Module: A simplified, 4-pin only version of the ZS-042 RTC module based on the DS3231 chip.
  ESP32-WROOM-32: A simplified ESP32-WROOM-32 part with less text on the PCB.
  Terminal Block - 2 pins: Generic Screw Terminal 8mm
